// Logisim project H2.circ as structural Verilog: 2 circuits, main circuit P2
module P2 (
  input  S1,
  input  S0,
  input  In,
  output S1n,
  output S0n,
  output Out
);

  wire and_1_out, and_2_out, and_3_out, and_4_out, and_5_out, and_6_out, and_7_out;

  and and_1 (and_1_out, ~In, ~S0, ~S1);  // AND_Gate
  and and_2 (and_2_out, In, ~S0, ~S1);  // AND_Gate
  and and_3 (and_3_out, ~In, S0, ~S1);  // AND_Gate
  and and_4 (and_4_out, In, S0, ~S1);  // AND_Gate
  and and_5 (and_5_out, ~In, ~S0, S1);  // AND_Gate
  and and_6 (and_6_out, ~In, S0, S1);  // AND_Gate
  and and_7 (and_7_out, In, S0, S1);
  or or_1 (S1n, and_1_out, and_6_out, and_5_out);
  or or_2 (S0n, and_2_out, and_5_out, and_4_out);
  or or_3 (Out, and_2_out, and_5_out, and_3_out, and_7_out, and_6_out);

  // Notes on the sheet:
  //   PROBLEM 2: IMPLEMENTING A STATE TABLE
  //   INPUT SECTION: Do not change anything here!
  //   You may only change the values of the inputs for testing using the hand tool.
  //   Do not introduce any other input or output pins in the circuit.
  //   To your logic
  //   OUTPUT SECTION: Do not change anything here!
  //   Do not introduce any other input or output pins in the circuit.
  //   From your logic
endmodule

module P3 (
  input  In,
  output Out
);

  wire and_1_out, and_2_out, and_3_out, and_4_out, and_5_out, and_6_out, and_7_out, and_8_out, and_9_out,
       clock_1_out, S0, S0n, S1, S1n, S2, S2n;

  Clock clock_1 (.out(clock_1_out));
  D_Flip_Flop u_S0 (.clk(clock_1_out), .D(S0n), .Q(S0));  // open: Qn, preset, en, reset
  D_Flip_Flop u_S1 (.clk(clock_1_out), .D(S1n), .Q(S1));  // open: Qn, preset, en, reset
  D_Flip_Flop u_S2 (.clk(clock_1_out), .D(S2n), .Q(S2));  // open: Qn, preset, en, reset
  and and_1 (and_1_out, ~In, ~S0, ~S1, ~S2);  // AND_Gate
  and and_2 (and_2_out, ~In, S0, ~S1, ~S2);  // AND_Gate
  and and_3 (and_3_out, In, S0, ~S1, ~S2);  // AND_Gate
  and and_4 (and_4_out, ~In, ~S0, S1, ~S2);  // AND_Gate
  and and_5 (and_5_out, ~In, S0, S1, ~S2);  // AND_Gate
  and and_6 (and_6_out, In, S0, S1, ~S2);  // AND_Gate
  and and_7 (and_7_out, ~In, ~S0, ~S1, S2);  // AND_Gate
  and and_8 (and_8_out, ~In, S0, ~S1, S2);  // AND_Gate
  and and_9 (and_9_out, ~In, ~S0, S1, S2);  // AND_Gate
  or or_1 (Out, and_8_out, and_9_out);
  or or_2 (S0n, and_3_out, and_4_out, and_8_out, and_2_out);
  or or_3 (S1n, and_6_out, and_7_out, and_8_out);
  or or_4 (S2n, and_1_out, and_2_out, and_5_out, and_6_out, and_9_out);

  // Notes on the sheet:
  //   PROBLEM 3: IMPLEMENTING A STATE MACHINE
  //   INPUT SECTION: Do not change anything here!
  //   You may only change the values of the inputs for testing using the hand tool.
  //   Do not introduce any other input or output pins in the circuit.
  //   To your logic
  //   OUTPUT SECTION: Do not change anything here!
  //   Do not introduce any other input or output pins in the circuit.
  //   From your logic
endmodule
